# Fritzing sketch DrkRmSign (saved by Fritzing 1.0.1rc)
breadboards: 1

parts:
  Part2 = Arduino Pro Micro (Clone)
  S1 = Taiway 100-SP-X-T1 SPDT Miniature Toggle Switch [part_number=100-SP-X-T1-0-0-B1-M2 package=THT]
  S2 = Momentary Switch [package=ksa_sealed_tac_switch]
  U1 = WS2812 RGB LED strip
  R1 = Rotary Potentiometer (Small) [maximum_resistance=10kΩ knob_status=50% power=0.5W package=THT]

nets:
  GND: Part2.GND, S1.COM, S2.4, U1.GND, R1.leg1
  N1: Part2.D5, S2.2
  N2: Part2.D6, U1.DIN
  N3: Part2.D8, S1.L1
  N4: Part2.D9, S1.L2
  N5: Part2.A3, R1.wiper
  5V: Part2.VCC, U1.VCC, R1.leg2

custom parts:
  WS2812 RGB LED strip: WS2812 strip
